# Fritzing sketch climatic-eye-schematic (saved by Fritzing 0.9.5d)

parts:
  CPU1 = NodeMCU WROOM ESP 32
  BMP280_Breakout1 = BMP280 Breakout Board [part_number=BMP280]
  YL-83_-_Detection_Board1 = YL-83 Rain Sensor - Detection Board
  YL-83_-_Control_Board1 = YL-83 Rain Sensor - Control Board
  BH1750FVI_Breakout1 = BH1750 (GY-302) Breakout Board [part_number=BH1750FVI]
  Part1 = FC-28 Soil Hygrometer Module - Probe
  Part2 = FC-28 Soil Hygrometer Module
  A3 = u-blox NEO-6M GPS Breakout
  DHT1 = DHT11 Humitidy and Temperature Sensor (3 pins)
  M1 = Osoyoo SX1278-ra-02
  PV1 = Generic Small 6V Solar Panel
  PV2 = Generic Small 6V Solar Panel
  TP1 = TP4056 [chip_label=TP4056 package="DIP (Dual Inline) [THT]"]
  BAT1 = Battery Holders [package=lipo-1100mAh]
  A4 = TPS61023
  ANT1 = Antenna  # not connected

nets:
  N1: CPU1.pin_5, YL-83_-_Control_Board1.AO
  N2: CPU1.pin_6, Part2.AO
  N3: CPU1.pin_10, M1.DIO0
  N4: CPU1.pin_11, DHT1.Signal
  N5: CPU1.pin_12, M1.RST
  N6: CPU1.pin_15, TP1.pin3, A4.Pin_2
  N7: CPU1.pin_16, A3.Pin_1, A4.Pin_3
  VCC: CPU1.pin_17, BMP280_Breakout1.VCC, YL-83_-_Control_Board1.VCC, BH1750FVI_Breakout1.VCC, Part2.VCC, DHT1.Plus, M1.3.3V
  GND: CPU1.pin_18, BMP280_Breakout1.GND, YL-83_-_Control_Board1.GND, BH1750FVI_Breakout1.GND, Part2.GND, A3.Pin_2, DHT1.Gnd, M1.GND
  N8: CPU1.pin_24, CPU1.pin_28, A3.Pin_3, M1.NSS
  N9: CPU1.pin_25, M1.SCK
  N10: CPU1.pin_26, M1.MISO
  N11: CPU1.pin_27, BMP280_Breakout1.SDA, BH1750FVI_Breakout1.SDA
  N12: CPU1.pin_29, A3.Pin_4
  N13: CPU1.pin_30, BMP280_Breakout1.SCL, BH1750FVI_Breakout1.SCL
  N14: YL-83_-_Detection_Board1.POS, YL-83_-_Control_Board1.POS
  N15: YL-83_-_Detection_Board1.NEG, YL-83_-_Control_Board1.NEG
  N16: Part1.POS, Part2.POS
  N17: Part1.NEG, Part2.NEG
  N18: PV1.+, PV2.+, TP1.pin1
  N19: PV1.-, PV2.-, TP1.pin2
  N20: TP1.pin4, BAT1.+
  N21: TP1.pin5, BAT1.-
  N22: TP1.pin6, A4.Pin_1

custom parts:
  NodeMCU WROOM ESP 32: 30 pol Development Kit
  BMP280 Breakout Board: This is a breakout board for the Bosch Sensortec BMP280, "an absolute barometric pressure sensor especially designed for mobile applications." The operation range is 300 to 1100 hPa. Supply voltage is 1.2 to 3.6V. Operating temperature range is -40 to +85 °C.
  YL-83 Rain Sensor - Detection Board: The YL-83 is a rain sensor that has more resistance when dry and less resistance when wet. The module runs at 5V.
  YL-83 Rain Sensor - Control Board: The YL-83 is a rain sensor that has more resistance when dry and less resistance when wet. The module runs at 5V.
  BH1750 (GY-302) Breakout Board: The ROHM Semiconductor BH1750FVI is a digital ambient light sensor for the I2C bus interface. The BH750FVI is able to detect a wide range of light intensities (1-65535 lux). The spectral range is similar to that of the human eye.
  FC-28 Soil Hygrometer Module - Probe: The FC-28 is a soil hygrometer module that uses the Texas Instruments LM393 comparator chip to provide an analog measurement of soil humidity.
  FC-28 Soil Hygrometer Module: The FC-28 is a soil hygrometer module that uses the Texas Instruments LM393 comparator chip to provide an analog measurement of soil humidity. The digital output is high when soil moisture is over a certain threshold, as determined by adjusting the potentiometer.
  DHT11 Humitidy and Temperature Sensor (3 pins): DHT11 Humidity and Temperature Sensor (3 pins).
  Osoyoo SX1278-ra-02: Osoyoo Long Distance wireless transceiver Uart LoRa Module.
  TP4056: A DIP stand-in part for whatever IC you want. With 6 pins on a 300mil dual inline package (DIP) footprint.
  TPS61023: Adafruit MiniBoost 5V @ 1A - TPS61023.
